# Fritzing sketch Wiring (saved by Fritzing 0.9.3b)
breadboards: 1

parts:
  Raspberry_Pi_2 = Raspberry Pi 3 [part_number=RPI-3-V1.2]
  Bauteil1 = Arduino Nano (Rev3.0) (ICSP)
  ISO_IN = DB25F
  ISO_OUT = DB25F
  TRRS1 = Audio Jack (TRRS) 3.5mm [part_number="LUMBERG JEITA RC-5325A" package="RC-5325A [SMD]"]

nets:
  N1: Raspberry_Pi_2.GPIO2, Bauteil1.A4
  N2: Raspberry_Pi_2.GPIO3, Bauteil1.A5
  GND: Raspberry_Pi_2.GND, Bauteil1.GND
  5V: Raspberry_Pi_2.5V, Bauteil1.5V
  N3: Bauteil1.D11/MOSI, ISO_OUT.pin13
  N4: Bauteil1.D12/MISO, ISO_OUT.pin12
  N5: Bauteil1.VIN, ISO_IN.pin12
  N6: Bauteil1.A0, ISO_IN.pin11, ISO_OUT.pin3
  N7: Bauteil1.D13/SCK, ISO_OUT.pin11
  N8: ISO_IN.pin13, ISO_OUT.pin1
  N9: ISO_OUT.pin9, TRRS1.TIP
  N10: ISO_OUT.pin10, TRRS1.RING2
  N11: ISO_OUT.pin22, TRRS1.SLEEVE
